// Digital circuit UTS.1.10.dig as structural Verilog
module UTS_1_10 (
  input  W,
  input  X,
  input  Y,
  input  Z,
  output OUTPUT
);

  wire and_1_out, and_2_out, and_3_out, and_4_out, and_5_out, not_1_out, not_2_out, not_3_out;

  not not_1 (not_1_out, W);
  not not_2 (not_2_out, X);
  not not_3 (not_3_out, Z);
  and and_1 (and_1_out, W, X, Y);
  and and_2 (and_2_out, W, not_2_out);
  and and_3 (and_3_out, W, not_2_out, Y);
  and and_4 (and_4_out, W, X, Y, Z);
  and and_5 (and_5_out, not_1_out, Y, not_3_out);
  or or_1 (OUTPUT, and_1_out, and_2_out, and_5_out, and_3_out, and_4_out);

  // Notes on the sheet:
  //   TEKOM KELAS A SALSALIM SULAIMAN
  //   WXYZ + WX '  + WX ' Y + WXY + W ' YZ '
endmodule
