// Digital circuit UTS.1.2.dig as structural Verilog
module UTS_1_2 (
  input  A,
  input  B,
  input  C,
  input  D,
  output OUTPUT
);

  wire and_1_out, and_2_out, and_3_out, and_4_out, and_5_out, and_6_out, not_1_out, not_2_out, not_3_out,
       not_4_out;

  not not_1 (not_1_out, A);
  not not_2 (not_2_out, B);
  not not_3 (not_3_out, C);
  not not_4 (not_4_out, D);
  and and_1 (and_1_out, not_1_out, not_2_out, not_3_out);
  and and_2 (and_2_out, not_1_out, C, D);
  and and_3 (and_3_out, not_1_out, not_3_out, not_4_out);
  and and_4 (and_4_out, not_1_out, B, D);
  and and_5 (and_5_out, A, B, C);
  and and_6 (and_6_out, A, not_2_out, C);
  or or_1 (OUTPUT, and_6_out, and_1_out, and_4_out, and_2_out, and_5_out, and_3_out);

  // Notes on the sheet:
  //   TEKOM KELAS A SALSALIM SULAIMAN
  //   A ' B ' C ' + A ' CD + A ' C ' D ' + A ' BD + ABC + AB ' C
endmodule
