// Digital circuit UTS.1.3.dig as structural Verilog
module UTS_1_3 (
  input  X,
  input  Y,
  input  Z,
  output OUTPUT
);

  wire and_1_out, and_2_out, and_3_out, not_1_out, not_2_out, not_3_out;

  not not_1 (not_1_out, X);
  not not_2 (not_2_out, Y);
  not not_3 (not_3_out, Z);
  and and_1 (and_1_out, not_1_out, not_2_out, not_3_out);
  and and_2 (and_2_out, Y, not_3_out);
  and and_3 (and_3_out, X, Y);
  or or_1 (OUTPUT, and_3_out, and_1_out, and_2_out);

  // Notes on the sheet:
  //   TEKOM KELAS A SALSALIM SULAIMAN
  //   X ' Y ' Z ' + YZ ' + XY
endmodule
