// Digital circuit UTS.1.4.dig as structural Verilog
module UTS_1_4 (
  input  A,
  input  B,
  input  C,
  input  D,
  output OUTPUT
);

  wire and_1_out, and_2_out, and_3_out, not_1_out, not_2_out;

  not not_1 (not_1_out, A);
  not not_2 (not_2_out, B);
  and and_1 (and_1_out, not_1_out, B);
  and and_2 (and_2_out, not_1_out, not_2_out);
  and and_3 (and_3_out, C, D);
  or or_1 (OUTPUT, and_1_out, and_2_out, and_3_out);

  // Notes on the sheet:
  //   TEKOM KELAS A SALSALIM SULAIMAN
  //   A ' B + A ' B ' C + CD
endmodule
