// Digital circuit UTS.1.8.dig as structural Verilog
module UTS_1_8 (
  input  A,
  input  B,
  input  C,
  input  D,
  output OUTPUT
);

  wire and_1_out, and_2_out, and_3_out, and_4_out, and_5_out, not_1_out, not_2_out, not_3_out;

  not not_1 (not_1_out, A);
  not not_2 (not_2_out, A);
  not not_3 (not_3_out, D);
  and and_1 (and_1_out, not_1_out, A, not_3_out);
  and and_2 (and_2_out, A, A, A);
  and and_3 (and_3_out, A, A, D);
  and and_4 (and_4_out, A, A, not_2_out);
  and and_5 (and_5_out, A, D);
  or or_1 (OUTPUT, and_1_out, and_2_out, and_5_out, and_3_out, and_4_out);

  assign B = A;
  assign C = A;

  // Notes on the sheet:
  //   TEKOM KELAS A SALSALIM SULAIMAN
  //   A ' BD ' + BDC + ABC ' + BD + ABC
endmodule
